# Fritzing sketch skema (saved by Fritzing 0.8.7b)

parts:
  U1 = ESP8266 NodeMCU LoLin module
  Part3 = SRF05 Ultrasonic Rangefinder
  LCM1602_IIC2 = LCM1602 IIC [part_number="LCM1602 IIC" chip_label="LCM1602 IIC" package="DIP (Dual Inline) [THT]"]
  U2 = LCD-16X2 [package=lcd-16x2]
  U3 = SWITCH_SPDT [package=kps-1290]  # not connected
  VCC1 = Battery block 9V

nets:
  N1: U1.D1, LCM1602_IIC2.SCL
  N2: U1.D2, LCM1602_IIC2.SDA
  N3: U1.D5, Part3.Echo
  N4: U1.D6, Part3.Trig
  VIN: U1.Vin, Part3.VCC
  GND: U1.GND, Part3.GND
  VSS: LCM1602_IIC2.VSS, U2.VSS
  N5: LCM1602_IIC2.V0, U2.VO
  N6: LCM1602_IIC2.RS, U2.RS
  N7: LCM1602_IIC2.RW, U2.R_W
  N8: LCM1602_IIC2.E, U2.E
  N9: LCM1602_IIC2.D0, U2.DB0
  N10: LCM1602_IIC2.D1, U2.DB1
  N11: LCM1602_IIC2.D2, U2.DB2
  N12: LCM1602_IIC2.D3, U2.DB3
  N13: LCM1602_IIC2.D4, U2.DB4
  N14: LCM1602_IIC2.D5, U2.DB5
  N15: LCM1602_IIC2.D6, U2.DB6
  N16: LCM1602_IIC2.D7, U2.DB7
  N17: LCM1602_IIC2.A, U2.A
  N18: LCM1602_IIC2.K, U2.K
  N19: LCM1602_IIC2.GND, VCC1.-
  N20: LCM1602_IIC2.LED_A, LCM1602_IIC2.LED_B

custom parts:
  ESP8266 NodeMCU LoLin module: ESP8266 based NodeMCU
  LCM1602 IIC: I2C-Module to use a 1602 or 2004 LCD on with the wire.h libory Serial LCD Modul
